// Logisim project LAB02.circ as structural Verilog
module Codificador_8_3 (
  input  X7,
  input  X6,
  input  X5,
  input  X4,
  input  X3,
  input  X2,
  input  X1,
  input  X0,
  output Z2,
  output Z1,
  output Z0
);

  or or_1 (Z2, X7, X6, X5, X4);
  or or_2 (Z1, X7, X6, X3, X2);
  or or_3 (Z0, X7, X5, X3, X1);
endmodule

module Decofidicador_2_4 (
  input  A1,
  input  A0,
  input  Habilitador,
  output Z0,
  output Z1,
  output Z2,
  output Z3
);

  wire and_1_out, and_2_out, and_3_out, and_4_out;

  and and_1 (and_1_out, ~A1, ~A0);  // AND_Gate
  and and_2 (and_2_out, ~A1, A0);  // AND_Gate
  and and_3 (and_3_out, A1, ~A0);  // AND_Gate
  and and_4 (and_4_out, A1, A0);
  and and_5 (Z0, and_1_out, Habilitador);
  and and_6 (Z1, and_2_out, Habilitador);
  and and_7 (Z2, and_3_out, Habilitador);
  and and_8 (Z3, and_4_out, Habilitador);
endmodule

module Conversor_Jhonson (
  input  x2,
  input  x1,
  input  x0,
  output y3,
  output y2,
  output y1,
  output y0
);

  wire and_1_out, and_2_out, and_3_out, and_4_out, and_5_out, and_6_out, and_7_out, and_8_out, not_1_out,
       not_2_out, not_3_out, not_4_out, not_5_out, not_6_out, not_7_out, not_8_out, not_9_out;

  not not_1 (not_1_out, x2);
  not not_2 (not_2_out, x1);
  not not_3 (not_3_out, x0);
  not not_4 (not_4_out, x2);
  not not_5 (not_5_out, x1);
  not not_6 (not_6_out, x2);
  not not_7 (not_7_out, x2);
  not not_8 (not_8_out, x1);
  not not_9 (not_9_out, x0);
  and and_1 (and_1_out, not_1_out, x1, x0);
  and and_2 (and_2_out, x2, not_2_out);
  and and_3 (and_3_out, x2, not_3_out);
  and and_4 (and_4_out, not_4_out, x1);
  and and_5 (and_5_out, x2, not_5_out);
  and and_6 (and_6_out, not_6_out, x0);
  and and_7 (and_7_out, not_7_out, x1);
  and and_8 (and_8_out, x2, not_8_out, not_9_out);
  or or_1 (y2, and_1_out, and_2_out, and_3_out);
  or or_2 (y1, and_4_out, and_5_out);
  or or_3 (y0, and_6_out, and_7_out, and_8_out);

  assign y3 = x2;
endmodule

module BlocoLogicoJhonson (
  input  x2,
  input  x1,
  input  x0,
  output y3,
  output y2,
  output y1,
  output y0
);

  Conversor_Jhonson conversor_jhonson_1 (.x2(x2), .x1(x1), .x0(x0), .y3(y3), .y2(y2), .y1(y1), .y0(y0));
endmodule

module \Aplicação_Codificador  (
  input  X7,
  input  X6,
  input  X5,
  input  X4,
  input  X3,
  input  X2,
  input  X1,
  input  X0,
  output Z2,
  output Z1,
  output Z0
);

  Codificador_8_3 codificador_8_3_1 (
    .X7(X7), .X6(X6), .X5(X5), .X4(X4), .X3(X3), .X2(X2), .X1(X1), .X0(X0), .Z2(Z2), .Z1(Z1), .Z0(Z0));

  // Notes on the sheet:
  //   Mensagem
  //   Aplicação
  //   Codificar (Enxugar)
  //   Mensagem Codificada
endmodule

module \Aplicação_Decodificador  (
  input  A1,
  input  A0,
  input  Habilitador,
  output Z0,
  output Z1,
  output Z2,
  output Z3
);

  Decofidicador_2_4 decofidicador_2_4_1 (
    .A1(A1), .A0(A0), .Habilitador(Habilitador), .Z0(Z0), .Z1(Z1), .Z2(Z2), .Z3(Z3));

  // Notes on the sheet:
  //   Mensagem Decodificada
  //   Aplicação
  //   Decodificar
  //   Mensagem
endmodule
