// Logisim project LAB03.circ as structural Verilog
module DiagramaLogicoMux2_1 (
  input  D0,
  input  D1,
  input  Controle,
  output Y
);

  wire and_1_out, and_2_out;

  and and_1 (and_1_out, D0, ~Controle);  // AND_Gate
  or or_1 (Y, and_1_out, and_2_out);
  and and_2 (and_2_out, D1, Controle);

  // Notes on the sheet:
  //   MUX 2:1 - Diagrama Lógico
endmodule

module BlocoLogicoMux2_1 (
  input  D0,
  input  D1,
  input  Controle,
  output Y
);

  DiagramaLogicoMux2_1 MUX_2_1 (.D0(D0), .D1(D1), .Controle(Controle), .Y(Y));

  // Notes on the sheet:
  //   MUX 2:1 - Bloco Lógico
endmodule

module DiagramaLogicoMux4_1 (
  input  D0,
  input  D1,
  input  D2,
  input  D3,
  input  C1,
  input  C0,
  output Y
);

  wire and_1_out, and_2_out, and_3_out, and_4_out, and_5_out, and_6_out, or_1_out, or_2_out;

  and and_1 (and_1_out, D0, ~C0);  // AND_Gate
  or or_1 (or_1_out, and_1_out, and_2_out);
  and and_2 (and_2_out, D1, C0);
  and and_3 (and_3_out, D2, ~C0);  // AND_Gate
  or or_2 (or_2_out, and_3_out, and_4_out);
  and and_4 (and_4_out, D3, C0);
  and and_5 (and_5_out, or_1_out, ~C1);  // AND_Gate
  and and_6 (and_6_out, or_2_out, C1);
  or or_3 (Y, and_5_out, and_6_out);

  // Notes on the sheet:
  //   MUX 4:1 - Diagrama Lógico
endmodule

module BlocoLogicoMux4_1 (
  input  D0,
  input  D1,
  input  D2,
  input  D3,
  input  C1,
  input  C0,
  output Y
);

  DiagramaLogicoMux4_1 MUX_4_1 (.D0(D0), .D1(D1), .D2(D2), .D3(D3), .C1(C1), .C0(C0), .Y(Y));

  // Notes on the sheet:
  //   MUX 4:1 - Bloco Lógico
endmodule

module DiagramaLogicoMux8_1 (
  input  D0,
  input  D1,
  input  D2,
  input  D3,
  input  S,
  input  D4,
  input  D5,
  input  D6,
  input  D7,
  input  C2,
  input  C1,
  input  C0,
  output Y,
  output W
);

  wire and_1_out, and_2_out, and_3_out, and_4_out, and_5_out, and_6_out, and_7_out, and_8_out, and_9_out,
       and_10_out, and_11_out, and_12_out, and_13_out, and_14_out, and_15_out, and_16_out, and_17_out,
       and_18_out, or_1_out, or_2_out, or_3_out, or_4_out, or_5_out, or_6_out, or_7_out, or_8_out;

  and and_1 (and_1_out, D4, ~C0);  // AND_Gate
  and and_2 (and_2_out, D5, C0);
  and and_3 (and_3_out, D6, ~C0);  // AND_Gate
  and and_4 (and_4_out, D7, C0);
  and and_5 (and_5_out, D0, ~C0);  // AND_Gate
  or or_1 (or_1_out, and_5_out, and_6_out);
  and and_6 (and_6_out, D1, C0);
  and and_7 (and_7_out, D2, ~C0);  // AND_Gate
  or or_2 (or_2_out, and_7_out, and_8_out);
  and and_8 (and_8_out, D3, C0);
  or or_3 (or_3_out, and_1_out, and_2_out);
  or or_4 (or_4_out, and_3_out, and_4_out);
  and and_9 (and_9_out, or_1_out, ~C1);  // AND_Gate
  and and_10 (and_10_out, or_2_out, C1);
  and and_11 (and_11_out, or_3_out, ~C1);  // AND_Gate
  or or_5 (or_5_out, and_11_out, and_12_out);
  and and_12 (and_12_out, or_4_out, C1);
  or or_6 (or_6_out, and_9_out, and_10_out);
  and and_13 (and_13_out, or_6_out, ~C2);  // AND_Gate
  and and_14 (and_14_out, or_5_out, C2);
  and and_15 (and_15_out, or_5_out, ~C2);  // AND_Gate
  and and_16 (and_16_out, C2, C2);
  or or_7 (or_7_out, and_13_out, and_14_out);
  or or_8 (or_8_out, and_15_out, and_16_out);
  and and_17 (and_17_out, or_7_out, ~S);  // AND_Gate
  and and_18 (and_18_out, or_8_out, S);
  or or_9 (Y, and_17_out, and_18_out);
  not not_1 (W, Y);
endmodule

module BlocoLogicoMux8_1 (
  input  D0,
  input  D1,
  input  D2,
  input  D3,
  input  D4,
  input  D5,
  input  D6,
  input  S,
  input  D7,
  input  C2,
  input  C1,
  input  C0,
  output Y,
  output W
);

  DiagramaLogicoMux8_1 MUX_8_1 (
    .D0(D0), .D1(D1), .D2(D2), .D3(D3), .D4(D4), .D5(D5), .D6(D6), .D7(D7), .C2(C2), .C1(C1), .C0(C0), .S(S),
    .Y(Y), .W(W));

  // Notes on the sheet:
  //   MUX 8:1 - Bloco Lógico
endmodule

module BlocoLogicoMux16_1_feitoDe4_1 (
  input  D0,
  input  D1,
  input  D2,
  input  D3,
  input  D4,
  input  D5,
  input  D6,
  input  D7,
  input  D8,
  input  D9,
  input  D10,
  input  D11,
  input  D12,
  input  D13,
  input  D14,
  input  D15,
  input  [1:0] \Seleção02 ,
  input  [1:0] \Seleção01 ,
  input  Enable,
  output Y
);

  wire multiplexer_1_out, multiplexer_2_out, multiplexer_3_out, multiplexer_4_out;

  Multiplexer #(.select(2)) multiplexer_1 (
    .in0(D0), .in1(D1), .in2(D2), .in3(D3), .out(multiplexer_1_out), .sel(\Seleção01 ), .en(Enable));
  Multiplexer #(.select(2)) multiplexer_2 (
    .in0(D4), .in1(D5), .in2(D6), .in3(D7), .out(multiplexer_2_out), .sel(\Seleção01 ), .en(Enable));
  Multiplexer #(.select(2)) multiplexer_3 (
    .in0(D8), .in1(D9), .in2(D10), .in3(D11), .out(multiplexer_3_out), .sel(\Seleção01 ), .en(Enable));
  Multiplexer #(.select(2)) multiplexer_4 (
    .in0(D12), .in1(D13), .in2(D14), .in3(D14), .out(multiplexer_4_out), .sel(\Seleção01 ), .en(Enable));
  Multiplexer #(.select(2)) multiplexer_5 (
    .in0(multiplexer_1_out), .in1(multiplexer_2_out), .in2(multiplexer_3_out), .in3(multiplexer_4_out),
    .out(Y), .sel(\Seleção02 ), .en(Enable));

  assign D15 = D14;
endmodule

module BlocoLogicoMux16_1_lOGISIM (
  input  D0,
  input  D1,
  input  D2,
  input  D3,
  input  D4,
  input  D5,
  input  D6,
  input  D7,
  input  D8,
  input  D9,
  input  D10,
  input  D11,
  input  Enable,
  input  [3:0] \Seleção ,
  input  D12,
  input  D13,
  input  D14,
  input  D15,
  output Y
);

  Multiplexer #(.select(4)) multiplexer_1 (
    .in0(D0), .in1(D1), .in2(D2), .in3(D3), .in4(D4), .in5(D5), .in6(D6), .in7(D7), .in8(D8), .in9(D9),
    .in10(D10), .in11(D11), .in12(D12), .in13(D13), .in14(D14), .in15(D15), .out(Y), .sel(\Seleção ),
    .en(Enable));

  // Notes on the sheet:
  //   MUX 16:1 - Existente no Logisim
endmodule

module DiagramaLogicoDemux_1_2 (
  input  \Seleção ,
  input  Enable,
  output S0,
  output S1
);

  and and_1 (S0, \Seleção , Enable);
  and and_2 (S1, Enable, ~\Seleção );  // AND_Gate

  // Notes on the sheet:
  //   DEMUX 1:2
endmodule

module BlocoLogicoDemux_1_2 (
  input  \Seleção ,
  input  Enable,
  output S0,
  output S1
);

  DiagramaLogicoDemux_1_2 DEMUX_1_2 (.\Seleção (\Seleção ), .Enable(Enable), .S0(S0), .S1(S1));
endmodule

module DiagramaLogicoDemux1_4 (
  input  Enable,
  input  C1,
  input  C2,
  output S0,
  output S1,
  output S2,
  output S3
);

  and and_1 (S0, Enable, ~C1, ~C2);  // AND_Gate
  and and_2 (S1, Enable, ~C1, C2);  // AND_Gate
  and and_3 (S2, Enable, C1, ~C2);  // AND_Gate
  and and_4 (S3, Enable, C1, C2);

  // Notes on the sheet:
  //   MUX 1:4
endmodule

module BlocoLogicoDemux1_4 (
  input  Enable,
  input  C1,
  input  C2,
  output S0,
  output S1,
  output S2,
  output S3
);

  DiagramaLogicoDemux1_4 MUX_1_4 (.Enable(Enable), .C1(C1), .C2(C2), .S0(S0), .S1(S1), .S2(S2), .S3(S3));
endmodule

module \DiagramaElétricoDemux1_4  (
  input  C1,
  input  C0,
  input  Enable,
  output S3,
  output S2,
  output S1,
  output S0
);

  wire n7400_1_pin8, n7400_1_pin11, n7408_1_pin2, n7408_1_pin12;

  _7400 #(.ShowInternalStructure("true")) u_7400_1 (
    .pin13(C1), .pin12(C1), .pin11(n7400_1_pin11), .pin10(C0), .pin9(C0), .pin8(n7400_1_pin8));  // open: pin1, pin2, pin3, pin4, pin5, pin6
  _7408 #(.ShowInternalStructure("true")) u_7408_1 (
    .pin1(n7400_1_pin8), .pin2(n7408_1_pin2), .pin3(S0), .pin4(C0), .pin5(n7408_1_pin2), .pin6(S1),
    .pin13(C0), .pin12(n7408_1_pin12), .pin11(S3), .pin10(n7400_1_pin8), .pin9(n7408_1_pin12), .pin8(S2));
  _7408 #(.ShowInternalStructure("true")) u_7408_2 (
    .pin13(C1), .pin12(Enable), .pin11(n7408_1_pin12), .pin10(n7400_1_pin11), .pin9(Enable),
    .pin8(n7408_1_pin2));  // open: pin1, pin2, pin3, pin4, pin5, pin6

  // Notes on the sheet:
  //   Diagrama Eletrico Demux 4:1
endmodule

module \Aplicação  (
  input  D0,
  input  D1,
  input  D2,
  input  D3,
  input  C1,
  input  C0,
  input  C1_2,
  input  C2,
  output S0,
  output S1,
  output S2,
  output S3
);

  wire MUX_4_1_y;

  DiagramaLogicoMux4_1 MUX_4_1 (.D0(D0), .D1(D1), .D2(D2), .D3(D3), .C1(C1), .C0(C0), .Y(MUX_4_1_y));
  DiagramaLogicoDemux1_4 MUX_1_4 (.Enable(MUX_4_1_y), .C1(C1_2), .C2(C2), .S0(S0), .S1(S1), .S2(S2), .S3(S3));

  // Notes on the sheet:
  //   APLICAÇÃO
endmodule
