// Logisim project LAB04.circ as structural Verilog
module \Detector_de_Paridade_Ímpar  (
  input  D,
  input  C,
  input  B,
  input  A,
  output Y
);

  wire and_1_out, and_2_out, and_3_out, and_4_out, and_5_out, and_6_out, and_7_out, and_8_out, not_1_out,
       not_2_out, not_3_out, not_4_out, not_5_out, not_6_out, not_7_out, not_8_out, not_9_out, not_10_out,
       not_11_out, not_12_out, not_13_out, not_14_out, not_15_out, not_16_out;

  not not_1 (not_1_out, D);
  not not_2 (not_2_out, C);
  not not_3 (not_3_out, B);
  not not_4 (not_4_out, A);
  not not_5 (not_5_out, D);
  not not_6 (not_6_out, C);
  not not_7 (not_7_out, D);
  not not_8 (not_8_out, B);
  not not_9 (not_9_out, D);
  not not_10 (not_10_out, A);
  not not_11 (not_11_out, C);
  not not_12 (not_12_out, B);
  not not_13 (not_13_out, C);
  not not_14 (not_14_out, A);
  not not_15 (not_15_out, B);
  not not_16 (not_16_out, A);
  and and_1 (and_1_out, not_1_out, not_2_out, not_3_out, not_4_out);
  and and_2 (and_2_out, not_5_out, not_6_out, B, A);
  and and_3 (and_3_out, not_7_out, C, not_8_out, A);
  and and_4 (and_4_out, not_9_out, C, B, not_10_out);
  and and_5 (and_5_out, D, not_11_out, not_12_out, A);
  and and_6 (and_6_out, D, not_13_out, B, not_14_out);
  and and_7 (and_7_out, D, C, not_15_out, not_16_out);
  and and_8 (and_8_out, D, C, B, A);
  or or_1 (Y, and_1_out, and_2_out, and_3_out, and_4_out, and_5_out, and_6_out, and_7_out, and_8_out);
endmodule

module Mux_8_1 (
  input  D,
  input  [2:0] C_B_A,
  output S
);

  wire not_1_out, not_2_out, not_3_out, not_4_out;

  not not_1 (not_1_out, D);
  not not_2 (not_2_out, D);
  not not_3 (not_3_out, D);
  not not_4 (not_4_out, D);
  Multiplexer #(.select(3), .enable("false")) multiplexer_1 (
    .in0(not_1_out), .in1(D), .in2(D), .in3(not_2_out), .in4(D), .in5(not_3_out), .in6(not_4_out), .in7(D),
    .out(S), .sel(C_B_A));
endmodule

module \Bloco_Lógico  (
  input  D,
  input  C,
  input  B,
  input  A,
  output S
);

  \Detector_de_Paridade_Ímpar  \detector_de_paridade_ímpar_1  (.D(D), .C(C), .B(B), .A(A), .Y(S));
endmodule

module \Somador_Binário  (
  input  A,
  input  B,
  input  C,
  output S0,
  output S1
);

  wire and_1_out, and_2_out, and_3_out, and_4_out, and_5_out, and_6_out, and_7_out, not_1_out, not_2_out,
       not_3_out, not_4_out, not_5_out, not_6_out;

  not not_1 (not_1_out, A);
  not not_2 (not_2_out, B);
  not not_3 (not_3_out, A);
  not not_4 (not_4_out, C);
  not not_5 (not_5_out, B);
  not not_6 (not_6_out, C);
  and and_1 (and_1_out, B, C);
  and and_2 (and_2_out, A, C);
  and and_3 (and_3_out, A, B);
  and and_4 (and_4_out, not_1_out, not_2_out, C);
  and and_5 (and_5_out, not_3_out, B, not_4_out);
  and and_6 (and_6_out, A, not_5_out, not_6_out);
  and and_7 (and_7_out, A, B, C);
  or or_1 (S1, and_1_out, and_2_out, and_3_out);
  or or_2 (S0, and_4_out, and_5_out, and_6_out, and_7_out);
endmodule

module BlocoLogicoSomador_4_bits (
  input  in_1,
  input  in_2,
  input  in_3,
  input  in_4,
  input  in_5,
  input  in_6,
  input  in_7,
  input  in_8,
  output out_9,
  output out_10,
  output out_11,
  output out_12
);

  wire \somador_binário_2_s1 , \somador_binário_3_s1 , \somador_binário_4_s1 ;

  \Somador_Binário  \somador_binário_1  (.A(in_1), .B(in_5), .C(\somador_binário_2_s1 ), .S0(out_9));  // open: S1
  \Somador_Binário  \somador_binário_2  (
    .A(in_2), .B(in_6), .C(\somador_binário_3_s1 ), .S0(out_10), .S1(\somador_binário_2_s1 ));
  \Somador_Binário  \somador_binário_3  (
    .A(in_3), .B(in_7), .C(\somador_binário_4_s1 ), .S0(out_11), .S1(\somador_binário_3_s1 ));
  \Somador_Binário  \somador_binário_4  (.A(in_4), .B(in_8), .C(1'b0), .S0(out_12), .S1(\somador_binário_4_s1 ));

  // Notes on the sheet:
  //   A
  //   S
  //   B
endmodule

module Detector_de_Estouro (
  input  A,
  input  B,
  input  R,
  output E
);

  wire and_1_out, and_2_out, not_1_out, not_2_out, not_3_out;

  not not_1 (not_1_out, A);
  not not_2 (not_2_out, B);
  not not_3 (not_3_out, R);
  and and_1 (and_1_out, not_1_out, not_2_out, R);
  and and_2 (and_2_out, A, B, not_3_out);
  or or_1 (E, and_1_out, and_2_out);
endmodule

module \Bloco_Lógico_Detector_Estouro  (
  input  A,
  input  B,
  input  R,
  output Estouro
);

  Detector_de_Estouro detector_de_estouro_1 (.A(A), .B(B), .R(R), .E(Estouro));
endmodule

module Flip_Flop_JK (
  input  J,
  input  K,
  input  CLEAR,
  output Q,
  output nQ
);

  wire CLOCK_out, not_1_out;

  Clock CLOCK (.out(CLOCK_out));
  not not_1 (not_1_out, CLEAR);
  J_K_Flip_Flop j_k_ff_1 (.J(J), .clk(CLOCK_out), .K(K), .Q(Q), .Qn(nQ), .reset(not_1_out));  // open: preset
endmodule
