// Logisim project LAB01A.circ as structural Verilog
module DiagramaLogicoAND3E (
  input  X0,
  input  X1,
  input  X2,
  output S
);

  and and_1 (S, X0, X1, X2);

  // Notes on the sheet:
  //   DIAGRAMA LOGICO - AND 3 ENTRADAS
endmodule

module BlocoLogicoAND3E (
  input  X0,
  input  X1,
  input  X2,
  output S
);

  DiagramaLogicoAND3E diagramalogicoand3e_1 (.X0(X0), .X1(X1), .X2(X2), .S(S));

  // Notes on the sheet:
  //   BLOCO LOGICO - AND 3 ENTRADAS
endmodule

module CircEquivComNAND (
  input  X0,
  input  X1,
  input  X2,
  output S
);

  wire nand_1_out;

  nand nand_1 (nand_1_out, X0, X1, X2);
  nand nand_2 (S, nand_1_out, nand_1_out, nand_1_out);

  // Notes on the sheet:
  //   DIAGRAMA LÓGICO
  //   AND 3 ENTRADAS FEITA COM PORTAS NAND
endmodule

module \AplicaçãoPráticaAND  (
  input  X0,
  input  X1,
  input  X2
);

  wire and_1_out;

  LED led_1 (.in(and_1_out));
  and and_1 (and_1_out, X0, X1, X2);

  // Notes on the sheet:
  //   Sinais Recebidos
  //   APLICAÇÃO PRÁTICA
  //   Abertura
endmodule

module DiagarmaLogicoXNORcomNAND (
  input  A0,
  input  A1,
  input  A2,
  input  B0,
  input  B1,
  input  B2,
  output S
);

  wire nand_1_out, nand_2_out, nand_3_out, nand_4_out, nand_5_out, nand_6_out, nand_7_out, nand_8_out,
       nand_9_out, nand_10_out, nand_11_out, nand_12_out, not_1_out, not_2_out, not_3_out, not_4_out,
       not_5_out, not_6_out, not_7_out, not_8_out;

  not not_1 (not_1_out, A0);
  not not_2 (not_2_out, B0);
  not not_3 (not_3_out, A1);
  not not_4 (not_4_out, B1);
  not not_5 (not_5_out, A2);
  not not_6 (not_6_out, B2);
  nand nand_1 (nand_1_out, not_1_out, not_2_out);
  nand nand_2 (nand_2_out, A0, B0);
  nand nand_3 (nand_3_out, not_3_out, not_4_out);
  nand nand_4 (nand_4_out, A1, B1);
  nand nand_5 (nand_5_out, not_5_out, not_6_out);
  nand nand_6 (nand_6_out, A2, B2);
  nand nand_7 (nand_7_out, nand_1_out, nand_2_out);
  nand nand_8 (nand_8_out, nand_3_out, nand_4_out);
  nand nand_9 (nand_9_out, nand_5_out, nand_6_out);
  nand nand_10 (nand_10_out, nand_7_out, nand_8_out);
  not not_7 (not_7_out, nand_10_out);
  not not_8 (not_8_out, nand_11_out);
  nand nand_11 (nand_11_out, nand_8_out, nand_9_out);
  not not_9 (S, nand_12_out);
  nand nand_12 (nand_12_out, not_7_out, not_8_out);

  // Notes on the sheet:
  //   XNOR COM NAND
endmodule

module BlocoLogioXNORcomNAND (
  input  A0,
  input  A1,
  input  A2,
  input  B0,
  input  B1,
  input  B2,
  output S
);

  DiagarmaLogicoXNORcomNAND diagarmalogicoxnorcomnand_1 (.A0(A0), .A1(A1), .A2(A2), .B0(B0), .B1(B1), .B2(B2), .S(S));
endmodule

module AplicacaoXNORcomNAND (
  input  CODIGO_0,
  input  CODIGO_1,
  input  CODIGO_2,
  input  RESPOTA_0,
  input  RESPOSTA_1,
  input  RESPOSTA_2,
  output Acesso_Liberado
);

  DiagarmaLogicoXNORcomNAND diagarmalogicoxnorcomnand_1 (
    .A0(CODIGO_0), .A1(CODIGO_1), .A2(CODIGO_2), .B0(RESPOTA_0), .B1(RESPOSTA_1), .B2(RESPOSTA_2),
    .S(Acesso_Liberado));

  // Notes on the sheet:
  //   APLICAÇÃO
  //   Senha de acesso
endmodule

module DiagramaLogicoComparador3BITS (
  input  A0,
  input  A1,
  input  A2,
  input  B0,
  input  B1,
  input  B2,
  output S
);

  wire nand_1_out, nand_2_out, nand_3_out, nand_4_out, nand_5_out, nand_6_out, nand_7_out, nand_8_out,
       nand_9_out, not_1_out, not_2_out, not_3_out, not_4_out, not_5_out, not_6_out;

  not not_1 (not_1_out, A0);
  not not_2 (not_2_out, B0);
  not not_3 (not_3_out, A1);
  not not_4 (not_4_out, B1);
  not not_5 (not_5_out, A2);
  not not_6 (not_6_out, B2);
  nand nand_1 (nand_1_out, not_1_out, not_2_out);
  nand nand_2 (nand_2_out, A0, B0);
  nand nand_3 (nand_3_out, not_3_out, not_4_out);
  nand nand_4 (nand_4_out, A1, B1);
  nand nand_5 (nand_5_out, not_5_out, not_6_out);
  nand nand_6 (nand_6_out, A2, B2);
  nand nand_7 (nand_7_out, nand_1_out, nand_2_out);
  nand nand_8 (nand_8_out, nand_3_out, nand_4_out);
  nand nand_9 (nand_9_out, nand_5_out, nand_6_out);
  and and_1 (S, nand_7_out, nand_8_out, nand_9_out);

  // Notes on the sheet:
  //   COMPARADOR DE 3 BITS
endmodule

module \AplicaçãoComparador3BITS  (
  input  Analogico_0,
  input  \Analógico_1 ,
  input  \Analógico_2 ,
  input  Digital_0,
  input  Digital_1,
  input  Digital_2,
  output Saida
);

  DiagramaLogicoComparador3BITS diagramalogicocomparador3bits_1 (
    .A0(Analogico_0), .A1(\Analógico_1 ), .A2(\Analógico_2 ), .B0(Digital_0), .B1(Digital_1), .B2(Digital_2),
    .S(Saida));

  // Notes on the sheet:
  //   Aplicação
  //   Conversão de sinais analógicos para Digitais
endmodule
