// Logisim project LAB01B.circ as structural Verilog
module DiagramaLogicoBASE (
  input  A,
  input  B,
  input  C,
  input  D,
  output S
);

  wire and_1_out, nor_1_out, or_1_out;

  and and_1 (and_1_out, B, C);
  or or_1 (or_1_out, C, D);
  nor nor_1 (nor_1_out, A, B);
  nand nand_1 (S, nor_1_out, and_1_out, or_1_out);
endmodule

module \DiagramElétricoBASE  (
  input  A,
  input  B,
  input  C,
  input  D,
  output S
);

  wire n7400_1_pin3, n7400_1_pin6, n7400_1_pin8, n7400_1_pin11, n7402_1_pin10, n7408_1_pin11, n7432_1_pin11;

  _7408 #(.ShowInternalStructure("true")) u_7408_1 (
    .pin13(C), .pin12(B), .pin11(n7408_1_pin11));  // open: pin1, pin2, pin3, pin4, pin5, pin6, pin10, pin9, pin8
  _7432 #(.ShowInternalStructure("true")) u_7432_1 (
    .pin13(D), .pin12(C), .pin11(n7432_1_pin11));  // open: pin1, pin2, pin3, pin4, pin5, pin6, pin10, pin9, pin8
  _7402 #(.ShowInternalStructure("true")) u_7402_1 (
    .pin10(n7402_1_pin10), .pin9(B), .pin8(A));  // open: pin1, pin2, pin3, pin4, pin5, pin6, pin13, pin12, pin11
  _7400 #(.ShowInternalStructure("true")) u_7400_1 (
    .pin1(n7408_1_pin11), .pin2(n7432_1_pin11), .pin3(n7400_1_pin3), .pin4(n7400_1_pin3),
    .pin5(n7400_1_pin3), .pin6(n7400_1_pin6), .pin13(n7408_1_pin11), .pin12(n7402_1_pin10),
    .pin11(n7400_1_pin11), .pin10(n7400_1_pin11), .pin9(n7400_1_pin11), .pin8(n7400_1_pin8));
  _7400 #(.ShowInternalStructure("true")) u_7400_2 (
    .pin13(n7400_1_pin6), .pin12(n7400_1_pin8), .pin11(S));  // open: pin1, pin2, pin3, pin4, pin5, pin6, pin10, pin9, pin8
endmodule

module DiagramaLogicoEquivNAND (
  input  A,
  input  B,
  input  C,
  input  D,
  output out_5
);

  wire nand_1_out, nand_2_out, nand_3_out, nand_4_out, nand_5_out, nand_6_out, nand_7_out, nand_8_out,
       nand_9_out, nand_10_out, nand_11_out, nand_12_out, nand_13_out;

  nand nand_1 (nand_1_out, B, C);
  nand nand_2 (nand_2_out, A, A);
  nand nand_3 (nand_3_out, B, B);
  nand nand_4 (nand_4_out, nand_1_out, nand_1_out);
  nand nand_5 (nand_5_out, C, C);
  nand nand_6 (nand_6_out, D, D);
  nand nand_7 (nand_7_out, nand_2_out, nand_3_out);
  nand nand_8 (nand_8_out, nand_5_out, nand_6_out);
  nand nand_9 (nand_9_out, nand_7_out, nand_7_out);
  nand nand_10 (nand_10_out, nand_9_out, nand_4_out);
  nand nand_11 (nand_11_out, nand_10_out, nand_10_out);
  nand nand_12 (nand_12_out, nand_4_out, nand_8_out);
  nand nand_13 (nand_13_out, nand_12_out, nand_12_out);
  nand nand_14 (out_5, nand_11_out, nand_13_out);
endmodule

module \DiagramaElétricoEquivNAND  (
  input  A,
  input  B,
  input  C,
  input  D,
  output S
);

  wire n7400_1_pin3, n7400_1_pin4, n7400_1_pin6, n7400_1_pin11, n7400_2_pin8, n7400_2_pin11, n7400_3_pin3,
       n7400_3_pin8, n7400_3_pin11, n7400_4_pin3, n7400_4_pin6, n7400_4_pin8, n7400_4_pin11;

  _7400 #(.ShowInternalStructure("true")) u_7400_1 (
    .pin1(B), .pin2(B), .pin3(n7400_1_pin3), .pin4(n7400_1_pin4), .pin5(n7400_1_pin4), .pin6(n7400_1_pin6),
    .pin13(A), .pin12(A), .pin11(n7400_1_pin11), .pin10(n7400_1_pin11), .pin9(n7400_1_pin3),
    .pin8(n7400_1_pin4));
  _7400 #(.ShowInternalStructure("true")) u_7400_2 (
    .pin13(C), .pin12(B), .pin11(n7400_2_pin11), .pin10(n7400_2_pin11), .pin9(n7400_2_pin11),
    .pin8(n7400_2_pin8));  // open: pin1, pin2, pin3, pin4, pin5, pin6
  _7400 #(.ShowInternalStructure("true")) u_7400_3 (
    .pin1(D), .pin2(D), .pin3(n7400_3_pin3), .pin13(C), .pin12(C), .pin11(n7400_3_pin11),
    .pin10(n7400_3_pin11), .pin9(n7400_3_pin3), .pin8(n7400_3_pin8));  // open: pin4, pin5, pin6
  _7400 #(.ShowInternalStructure("true")) u_7400_4 (
    .pin1(n7400_2_pin8), .pin2(n7400_3_pin8), .pin3(n7400_4_pin3), .pin4(n7400_4_pin3), .pin5(n7400_4_pin3),
    .pin6(n7400_4_pin6), .pin13(n7400_2_pin8), .pin12(n7400_1_pin6), .pin11(n7400_4_pin11),
    .pin10(n7400_4_pin11), .pin9(n7400_4_pin11), .pin8(n7400_4_pin8));
  _7400 #(.ShowInternalStructure("true")) u_7400_5 (
    .pin13(n7400_4_pin6), .pin12(n7400_4_pin8), .pin11(S));  // open: pin1, pin2, pin3, pin4, pin5, pin6, pin10, pin9, pin8
endmodule

module DiagramaLogicoEquivNOR (
  input  A,
  input  B,
  input  C,
  input  D,
  output out_5
);

  wire nor_1_out, nor_2_out, nor_3_out, nor_4_out, nor_5_out, nor_6_out, nor_7_out, nor_8_out, nor_9_out,
       nor_10_out, nor_11_out, nor_12_out, nor_13_out, nor_14_out;

  nor nor_1 (nor_1_out, A, B);
  nor nor_2 (nor_2_out, C, D);
  nor nor_3 (nor_3_out, B, B);
  nor nor_4 (nor_4_out, nor_3_out, nor_5_out);
  nor nor_5 (nor_5_out, C, C);
  nor nor_6 (nor_6_out, nor_2_out, nor_2_out);
  nor nor_7 (nor_7_out, nor_1_out, nor_1_out);
  nor nor_8 (nor_8_out, nor_4_out, nor_4_out);
  nor nor_9 (nor_9_out, nor_6_out, nor_6_out);
  nor nor_10 (nor_10_out, nor_7_out, nor_8_out);
  nor nor_11 (nor_11_out, nor_8_out, nor_9_out);
  nor nor_12 (nor_12_out, nor_10_out, nor_10_out);
  nor nor_13 (nor_13_out, nor_11_out, nor_11_out);
  nor nor_14 (nor_14_out, nor_12_out, nor_13_out);
  nor nor_15 (out_5, nor_14_out, nor_14_out);
endmodule

module \DiagramaElétricoEquivNOR  (
  input  A,
  input  B,
  input  C,
  input  D,
  output S
);

  wire n7402_1_pin10, n7402_2_pin1, n7402_2_pin2, n7402_2_pin3, n7402_3_pin1, n7402_3_pin2, n7402_4_pin4,
       n7402_4_pin10, n7402_4_pin13, n7402_5_pin1, n7402_5_pin2, n7402_5_pin12, n7402_5_pin13, n7402_6_pin2;

  _7402 #(.ShowInternalStructure("true")) u_7402_1 (
    .pin10(n7402_1_pin10), .pin9(B), .pin8(A));  // open: pin1, pin2, pin3, pin4, pin5, pin6, pin13, pin12, pin11
  _7402 #(.ShowInternalStructure("true")) u_7402_2 (
    .pin1(n7402_2_pin1), .pin2(n7402_2_pin2), .pin3(n7402_2_pin3), .pin4(n7402_2_pin3), .pin5(B), .pin6(B),
    .pin10(n7402_2_pin2), .pin9(C), .pin8(C));  // open: pin13, pin12, pin11
  _7402 #(.ShowInternalStructure("true")) u_7402_3 (
    .pin1(n7402_3_pin1), .pin2(n7402_3_pin2), .pin3(n7402_3_pin2), .pin4(n7402_3_pin2), .pin5(C), .pin6(D));  // open: pin13, pin12, pin11, pin10, pin9, pin8
  _7402 #(.ShowInternalStructure("true")) u_7402_4 (
    .pin4(n7402_4_pin4), .pin5(n7402_1_pin10), .pin6(n7402_1_pin10), .pin13(n7402_4_pin13),
    .pin12(n7402_3_pin1), .pin11(n7402_3_pin1), .pin10(n7402_4_pin10), .pin9(n7402_2_pin1),
    .pin8(n7402_2_pin1));  // open: pin1, pin2, pin3
  _7402 #(.ShowInternalStructure("true")) u_7402_5 (
    .pin1(n7402_5_pin1), .pin2(n7402_5_pin2), .pin3(n7402_5_pin2), .pin4(n7402_5_pin2), .pin5(n7402_4_pin4),
    .pin6(n7402_4_pin10), .pin13(n7402_5_pin13), .pin12(n7402_5_pin12), .pin11(n7402_5_pin12),
    .pin10(n7402_5_pin12), .pin9(n7402_4_pin13), .pin8(n7402_4_pin10));
  _7402 #(.ShowInternalStructure("true")) u_7402_6 (
    .pin1(S), .pin2(n7402_6_pin2), .pin3(n7402_6_pin2), .pin4(n7402_6_pin2), .pin5(n7402_5_pin1),
    .pin6(n7402_5_pin13));  // open: pin13, pin12, pin11, pin10, pin9, pin8
endmodule

module DetectorDeParidade (
  input  A,
  input  B,
  input  C,
  input  P,
  output S
);

  wire xor_1_out, xor_2_out;

  xor xor_1 (xor_1_out, A, B);
  xor xor_2 (xor_2_out, xor_1_out, C);
  xor xor_3 (S, xor_2_out, P);
endmodule

module \AplicaçãoDetectordeParidade  (
  input  A,
  input  B,
  input  C,
  input  Paridade_Receptor__PAR,
  output Erro
);

  wire xor_1_out, xor_2_out;

  xor xor_1 (xor_1_out, A, B);
  xor xor_2 (xor_2_out, xor_1_out, C);
  xor xor_3 (Erro, xor_2_out, Paridade_Receptor__PAR);
endmodule

module \ImplementaçãoDeFuncaoLogica  (
  input  A,
  input  B,
  input  C,
  input  D,
  output S
);

  wire or_1_out;

  or or_1 (or_1_out, A, B);
  and and_1 (S, or_1_out, D);
endmodule
