// Logisim project LAB05.circ as structural Verilog
module DiagramaLogicoRegistrador (
  input  D3,
  input  D2,
  input  D1,
  input  D0,
  input  Ent__Paralela,
  input  CLK,
  input  Dad__Entrada,
  output S,
  output S3,
  output S2,
  output S1,
  output S0
);

  wire j_k_ff_1_qn, j_k_ff_2_qn, j_k_ff_3_qn, multiplexer_1_out, multiplexer_2_out, multiplexer_3_out,
       multiplexer_4_out, not_1_out, not_2_out, not_3_out, not_4_out, not_5_out;

  not not_1 (not_1_out, Dad__Entrada);
  // AND_Gate and_1 has open pins: in0=Ent__Paralela, in1=not_2_out, out=open
  Multiplexer multiplexer_1 (.in0(1'b0), .in1(1'b1), .out(multiplexer_1_out), .sel(D3), .en(Ent__Paralela));
  J_K_Flip_Flop j_k_ff_1 (.J(Dad__Entrada), .clk(CLK), .K(not_1_out), .Q(S3), .Qn(j_k_ff_1_qn));  // open: preset, reset
  not not_2 (not_2_out, multiplexer_1_out);
  Multiplexer multiplexer_2 (.in0(1'b0), .in1(1'b1), .out(multiplexer_2_out), .sel(D2), .en(Ent__Paralela));
  not not_3 (not_3_out, multiplexer_2_out);
  // AND_Gate and_2 has open pins: in0=Ent__Paralela, in1=not_3_out, out=open
  J_K_Flip_Flop j_k_ff_2 (
    .J(S3), .clk(CLK), .K(j_k_ff_1_qn), .Q(S2), .Qn(j_k_ff_2_qn), .reset(multiplexer_2_out));  // open: preset
  not not_4 (not_4_out, multiplexer_3_out);
  // AND_Gate and_3 has open pins: in0=Ent__Paralela, in1=not_4_out, out=open
  Multiplexer multiplexer_3 (.in0(1'b0), .in1(1'b1), .out(multiplexer_3_out), .sel(D1), .en(Ent__Paralela));
  J_K_Flip_Flop j_k_ff_3 (
    .J(S2), .clk(CLK), .K(j_k_ff_2_qn), .Q(S1), .Qn(j_k_ff_3_qn), .reset(multiplexer_3_out));  // open: preset
  Multiplexer multiplexer_4 (.in0(1'b0), .in1(1'b1), .out(multiplexer_4_out), .sel(D0), .en(Ent__Paralela));
  not not_5 (not_5_out, multiplexer_4_out);
  // AND_Gate and_4 has open pins: in0=Ent__Paralela, in1=not_5_out, out=open
  J_K_Flip_Flop j_k_ff_4 (.J(S1), .clk(CLK), .K(j_k_ff_3_qn), .Q(S), .reset(multiplexer_4_out));  // open: Qn, preset

  assign S0 = S;
endmodule

module BlocoLogicoRegistrador (
  input  D3,
  input  D2,
  input  D1,
  input  D0,
  input  Ent__Paralela,
  input  Dad__Entrada,
  output S,
  output S3,
  output S2,
  output S1,
  output S0
);

  wire CLOCK_out;

  Clock CLOCK (.out(CLOCK_out));
  DiagramaLogicoRegistrador diagramalogicoregistrador_1 (
    .Ent__Paralela(Ent__Paralela), .CLK(CLOCK_out), .Dad__Entrada(Dad__Entrada), .D3(D3), .D2(D2), .D1(D1),
    .D0(D0), .S3(S3), .S2(S2), .S1(S1), .S0(S0), .S(S));
endmodule

module DiagramaLogicoContador (
  input  CLK,
  output S3,
  output S2,
  output S1,
  output S0
);

  wire and_1_out, j_k_ff_1_qn, j_k_ff_2_qn, j_k_ff_3_qn, not_1_out;

  not not_1 (not_1_out, CLK);
  J_K_Flip_Flop j_k_ff_1 (
    .J(1'b1), .clk(not_1_out), .K(1'b1), .Q(S0), .Qn(j_k_ff_1_qn), .reset(and_1_out));  // open: preset
  J_K_Flip_Flop j_k_ff_2 (
    .J(1'b1), .clk(j_k_ff_1_qn), .K(1'b1), .Q(S1), .Qn(j_k_ff_2_qn), .reset(and_1_out));  // open: preset
  J_K_Flip_Flop j_k_ff_3 (
    .J(1'b1), .clk(j_k_ff_2_qn), .K(1'b1), .Q(S2), .Qn(j_k_ff_3_qn), .reset(and_1_out));  // open: preset
  and and_1 (and_1_out, S2, S3);
  J_K_Flip_Flop j_k_ff_4 (.J(1'b1), .clk(j_k_ff_3_qn), .K(1'b1), .Q(S3), .reset(and_1_out));  // open: Qn, preset
endmodule

module BlocoLogicoContador (
  output S3,
  output S2,
  output S1,
  output S0
);

  wire CLOCK_out;

  DiagramaLogicoContador diagramalogicocontador_1 (.CLK(CLOCK_out), .S3(S3), .S2(S2), .S1(S1), .S0(S0));
  Clock CLOCK (.out(CLOCK_out));
endmodule

module \AplicaçãoFinal  (
  input  [3:0] Credito_da_Cadeira,
  input  [2:0] Disciplinas,
  output [3:0] Creditos_Totais,
  output [3:0] \Matrícula_Registrada 
);

  wire and_1_out, Matricular_out, multiplexer_2_out, \Registrar_Matrícula_out , xnor_1_out;
  wire [3:0] adder_1_out, multiplexer_1_out;

  Button Matricular (.out(Matricular_out));
  Button \Registrar_Matrícula  (.out(\Registrar_Matrícula_out ));
  Multiplexer #(.select(3), .width(4), .enable("false")) multiplexer_1 (
    .in0(Credito_da_Cadeira), .out(multiplexer_1_out), .sel(Disciplinas));  // open: in1, in2, in3, in4, in5, in6, in7
  Register #(.width(4), .Select("low")) register_1 (
    .D(adder_1_out), .Q(Creditos_Totais), .clk(Matricular_out), .clr(\Registrar_Matrícula_out ));  // open: en
  Adder #(.width(4)) adder_1 (.a(multiplexer_1_out), .b(Creditos_Totais), .out(adder_1_out));  // open: cin, cout
  and and_1 (and_1_out, 1'b1, multiplexer_2_out);
  Register #(.width(4), .Select("low")) register_2 (
    .D(Creditos_Totais), .Q(\Matrícula_Registrada ), .clk(\Registrar_Matrícula_out ));  // open: en, clr
  Multiplexer #(.select(4), .enable("false")) multiplexer_2 (
    .in0(1'b0), .in1(1'b0), .in2(1'b0), .in3(1'b0), .in4(1'b0), .in5(1'b0), .in6(1'b1), .in7(1'b1),
    .in8(1'b1), .in9(1'b1), .in10(1'b1), .in11(1'b1), .in12(1'b1), .in13(1'b0), .in14(1'b0), .in15(1'b0),
    .out(multiplexer_2_out), .sel(Creditos_Totais));
  xnor xnor_1 (xnor_1_out, multiplexer_2_out, 1'b0);
  // RGBLed Sinaliza_Matricula_Feita: pin names not known; wires that end beside it: xnor_1_out, and_1_out
endmodule
